// Logisim project sap2_main.circ as structural Verilog: 1 circuit, main circuit main
module main (
  output [15:0] out_1,
  output [15:0] out_2,
  output [15:0] out_3,
  output [3:0] out_4,
  output [2:0] out_5,
  output [7:0] out_6,
  output [15:0] out_7
);

  wire arithmetic_logic_unit_1_carry, arithmetic_logic_unit_1_sign, CLK, COUNT_PC, EN_ACC, EN_B, EN_C,
       EN_INS, EN_L, EN_MAR, EN_MDR, EN_MDRH, EN_PC, EN_RAM, EN_TEMP, EN_Z, LOAD1_Z, LOAD2_Z, LOAD_ACC,
       LOAD_B, LOAD_C, LOAD_FLAGS, LOAD_INS, LOAD_L, LOAD_MAR, LOAD_MDR, LOAD_PC, LOAD_RAM, LOAD_TEMP,
       nor_1_out, RESET;
  wire [3:0] OP;
  wire [7:0] ram_1_dout, register_8_1_q1, register_8_2_o1, register_8_3_o1;
  wire [15:0] register_16_1_q1;
  wire [31:31] rom_1_data;

  Clock clock_1 (.out(CLK));
  RAM #(.addrWidth(16), .asyncread("true")) ram_1 (
    .addr(register_16_1_q1), .we(LOAD_RAM), .oe(EN_RAM), .clk(CLK), .din(out_1[7:0]), .dout(ram_1_dout));
  pc pc_1 (.EN(EN_PC), .LOAD(LOAD_PC), .COUNT(COUNT_PC), .CLK(CLK), .D_in(out_1), .Q_out(out_1), .O_out(out_2));
  register_16 register_16_1 (
    .D1(out_1[0]), .D2(out_1[1]), .D3(out_1[2]), .D4(out_1[3]), .D5(out_1[4]), .D6(out_1[5]), .D7(out_1[6]),
    .D8(out_1[7]), .D9(out_1[8]), .D10(out_1[9]), .D11(out_1[10]), .D12(out_1[11]), .D13(out_1[12]),
    .D14(out_1[13]), .D15(out_1[14]), .D16(out_1[15]), .LOAD(LOAD_MAR), .CLK(CLK), .EN(EN_MAR),
    .O1(out_3[0]), .O2(out_3[1]), .O3(out_3[2]), .O4(out_3[3]), .O5(out_3[4]), .O6(out_3[5]), .O7(out_3[6]),
    .O8(out_3[7]), .O9(out_3[8]), .O10(out_3[9]), .O11(out_3[10]), .O12(out_3[11]), .O13(out_3[12]),
    .O14(out_3[13]), .O15(out_3[14]), .O16(out_3[15]), .Q1(register_16_1_q1[0]), .Q2(register_16_1_q1[1]),
    .Q3(register_16_1_q1[2]), .Q4(register_16_1_q1[3]), .Q5(register_16_1_q1[4]), .Q6(register_16_1_q1[5]),
    .Q7(register_16_1_q1[6]), .Q8(register_16_1_q1[7]), .Q9(register_16_1_q1[8]), .Q10(register_16_1_q1[9]),
    .Q11(register_16_1_q1[10]), .Q12(register_16_1_q1[11]), .Q13(register_16_1_q1[12]),
    .Q14(register_16_1_q1[13]), .Q15(register_16_1_q1[14]), .Q16(register_16_1_q1[15]));
  register_8 register_8_1 (
    .D1(ram_1_dout[0]), .D2(ram_1_dout[1]), .D3(ram_1_dout[2]), .D4(ram_1_dout[3]), .D5(ram_1_dout[4]),
    .D6(ram_1_dout[5]), .D7(ram_1_dout[6]), .D8(ram_1_dout[7]), .LOAD(LOAD_MDR), .CLK(CLK), .EN(EN_MDR),
    .Q1(register_8_1_q1[0]), .Q2(register_8_1_q1[1]), .Q3(register_8_1_q1[2]), .Q4(register_8_1_q1[3]),
    .Q5(register_8_1_q1[4]), .Q6(register_8_1_q1[5]), .Q7(register_8_1_q1[6]), .Q8(register_8_1_q1[7]));  // open: O1, O2, O3, O4, O5, O6, O7, O8
  Demultiplexer #(.tristate("true"), .width(8)) demultiplexer_1 (
    .out0(out_1[7:0]), .out1(out_1[15:8]), .in(register_8_1_q1), .sel(EN_MDRH));
  register_z16bits register_z16bits_1 (
    .D1(out_1[0]), .D2(out_1[1]), .D3(out_1[2]), .D4(out_1[3]), .D5(out_1[4]), .D6(out_1[5]), .D7(out_1[6]),
    .D8(out_1[7]), .D9(out_1[8]), .D10(out_1[9]), .D11(out_1[10]), .D12(out_1[11]), .D13(out_1[12]),
    .D14(out_1[13]), .D15(out_1[14]), .D16(out_1[15]), .CLK(CLK), .LOAD1(LOAD1_Z), .LOAD2(LOAD2_Z),
    .EN1(EN_Z), .EN2(EN_Z), .Q1(out_1[0]), .Q2(out_1[1]), .Q3(out_1[2]), .Q4(out_1[3]), .Q5(out_1[4]),
    .Q6(out_1[5]), .Q7(out_1[6]), .Q8(out_1[7]), .Q9(out_1[8]), .Q10(out_1[9]), .Q11(out_1[10]),
    .Q12(out_1[11]), .Q13(out_1[12]), .Q14(out_1[13]), .Q15(out_1[14]), .Q16(out_1[15]));  // open: O1, O2, O3, O4, O5, O6, O7, O8, O9, O10, O11, O12, O13, O14, O15, O16
  register_16 register_16_2 (
    .D1(out_1[0]), .D2(out_1[1]), .D3(out_1[2]), .D4(out_1[3]), .D5(out_1[4]), .D6(out_1[5]), .D7(out_1[6]),
    .D8(out_1[7]), .D9(out_1[8]), .D10(out_1[9]), .D11(out_1[10]), .D12(out_1[11]), .D13(out_1[12]),
    .D14(out_1[13]), .D15(out_1[14]), .D16(out_1[15]), .LOAD(LOAD_L), .CLK(CLK), .EN(EN_L), .Q1(out_1[0]),
    .Q2(out_1[1]), .Q3(out_1[2]), .Q4(out_1[3]), .Q5(out_1[4]), .Q6(out_1[5]), .Q7(out_1[6]), .Q8(out_1[7]),
    .Q9(out_1[8]), .Q10(out_1[9]), .Q11(out_1[10]), .Q12(out_1[11]), .Q13(out_1[12]), .Q14(out_1[13]),
    .Q15(out_1[14]), .Q16(out_1[15]));  // open: O1, O2, O3, O4, O5, O6, O7, O8, O9, O10, O11, O12, O13, O14, O15, O16
  register_8 register_8_2 (
    .D1(out_1[0]), .D2(out_1[1]), .D3(out_1[2]), .D4(out_1[3]), .D5(out_1[4]), .D6(out_1[5]), .D7(out_1[6]),
    .D8(out_1[7]), .LOAD(LOAD_ACC), .CLK(CLK), .EN(EN_ACC), .O1(register_8_2_o1[0]), .O2(register_8_2_o1[1]),
    .O3(register_8_2_o1[2]), .O4(register_8_2_o1[3]), .O5(register_8_2_o1[4]), .O6(register_8_2_o1[5]),
    .O7(register_8_2_o1[6]), .O8(register_8_2_o1[7]), .Q1(out_1[0]), .Q2(out_1[1]), .Q3(out_1[2]),
    .Q4(out_1[3]), .Q5(out_1[4]), .Q6(out_1[5]), .Q7(out_1[6]), .Q8(out_1[7]));
  register_8 register_8_3 (
    .D1(out_1[0]), .D2(out_1[1]), .D3(out_1[2]), .D4(out_1[3]), .D5(out_1[4]), .D6(out_1[5]), .D7(out_1[6]),
    .D8(out_1[7]), .LOAD(LOAD_TEMP), .CLK(CLK), .EN(EN_TEMP), .O1(register_8_3_o1[0]),
    .O2(register_8_3_o1[1]), .O3(register_8_3_o1[2]), .O4(register_8_3_o1[3]), .O5(register_8_3_o1[4]),
    .O6(register_8_3_o1[5]), .O7(register_8_3_o1[6]), .O8(register_8_3_o1[7]), .Q1(out_1[0]), .Q2(out_1[1]),
    .Q3(out_1[2]), .Q4(out_1[3]), .Q5(out_1[4]), .Q6(out_1[5]), .Q7(out_1[6]), .Q8(out_1[7]));
  register_8 register_8_4 (
    .D1(out_1[0]), .D2(out_1[1]), .D3(out_1[2]), .D4(out_1[3]), .D5(out_1[4]), .D6(out_1[5]), .D7(out_1[6]),
    .D8(out_1[7]), .LOAD(LOAD_B), .CLK(CLK), .EN(EN_B), .Q1(out_1[0]), .Q2(out_1[1]), .Q3(out_1[2]),
    .Q4(out_1[3]), .Q5(out_1[4]), .Q6(out_1[5]), .Q7(out_1[6]), .Q8(out_1[7]));  // open: O1, O2, O3, O4, O5, O6, O7, O8
  register_8 register_8_5 (
    .D1(out_1[0]), .D2(out_1[1]), .D3(out_1[2]), .D4(out_1[3]), .D5(out_1[4]), .D6(out_1[5]), .D7(out_1[6]),
    .D8(out_1[7]), .LOAD(LOAD_C), .CLK(CLK), .EN(EN_C), .Q1(out_1[0]), .Q2(out_1[1]), .Q3(out_1[2]),
    .Q4(out_1[3]), .Q5(out_1[4]), .Q6(out_1[5]), .Q7(out_1[6]), .Q8(out_1[7]));  // open: O1, O2, O3, O4, O5, O6, O7, O8
  register_8 register_8_6 (
    .D1(out_1[0]), .D2(out_1[1]), .D3(out_1[2]), .D4(out_1[3]), .D5(out_1[4]), .D6(out_1[5]), .D7(out_1[6]),
    .D8(out_1[7]), .LOAD(LOAD_INS), .CLK(CLK), .EN(EN_INS), .O1(out_6[0]), .O2(out_6[1]), .O3(out_6[2]),
    .O4(out_6[3]), .O5(out_6[4]), .O6(out_6[5]), .O7(out_6[6]), .O8(out_6[7]), .Q1(out_1[0]), .Q2(out_1[1]),
    .Q3(out_1[2]), .Q4(out_1[3]), .Q5(out_1[4]), .Q6(out_1[5]), .Q7(out_1[6]), .Q8(out_1[7]));
  ring ring_1 (.CLR(RESET), .CLK(CLK), .STATE(out_4));
  arithmetic_logic_unit arithmetic_logic_unit_1 (
    .A(register_8_2_o1), .B(register_8_3_o1), .OP(OP), .SIGN(arithmetic_logic_unit_1_sign), .Q(out_1[7:0]),
    .Carry(arithmetic_logic_unit_1_carry));
  nor nor_1 (nor_1_out, out_1[0], out_1[1], out_1[2], out_1[3], out_1[4], out_1[5], out_1[6], out_1[7]);
  ROM #(.addrWidth(16), .dataWidth(32)) rom_1 (
    .addr({out_6, out_4, 1'b0, out_5}),
    .data({rom_1_data[31], RESET, EN_INS, LOAD_INS, EN_C, LOAD_C, EN_B, LOAD_B, LOAD_FLAGS, OP, EN_TEMP, LOAD_TEMP, EN_ACC, LOAD_ACC, EN_L, LOAD_L, EN_Z, LOAD2_Z, LOAD1_Z, EN_MDRH, EN_MDR, LOAD_MDR, EN_RAM, LOAD_RAM, EN_MAR, LOAD_MAR, COUNT_PC, LOAD_PC, EN_PC}));
  flags flags_1 (
    .Carry(arithmetic_logic_unit_1_carry), .Sign(arithmetic_logic_unit_1_sign), .Zero(nor_1_out),
    .LOAD(LOAD_FLAGS), .CLK(CLK), .Carry_out(out_5[0]), .Sign_out(out_5[1]), .Zero_out(out_5[2]));

  assign out_7 = {out_6, out_4, 1'b0, out_5};

  // Other names for the same wires on the sheet: FLAG[2:0] = out_5

  // Notes on the sheet:
  //   Random Access Memory
  //   L Register
  //   Program Counter
  //   Memory Address Register
  //   Memory Data Register
  //    Z Register
  //   Accumulator Register
  //   Temporary Register
  //   Register B
  //   Register C
  //   Instruction Register
  //   contents of rom_1 (hex, n*v repeats v):
  //   8*9 8*0 8*d4 8*0 8*10000100 216*0 8*9 8*0 8*d4 8*0 8*10000100 216*0 8*9 8*0 8*d4 8*0 8*10000100
  //   216*0 8*9 8*0 8*d4 8*0 8*10000100 216*0 8*9 8*0 8*d4 8*0 8*10000100 216*0 8*9 8*0 8*d4 8*0
  //   8*10000100 216*0 8*9 8*0 8*d4 8*0 8*10000100 216*0 8*9 8*0 8*d4 8*0 8*10000100 216*0 8*9 8*0 8*d4
  //   8*0 8*10000100 216*0 8*9 8*0 8*d4 8*0 8*10000100 216*0 8*9 8*0 8*d4 8*0 8*10000100 216*0 8*9 8*0
  //   8*d4 8*0 8*10000100 216*0 8*9 8*0 8*d4 8*0 8*10000100 216*0 8*9 8*0 8*d4 8*0 8*10000100 216*0 8*9
  //   8*0 8*d4 8*0 8*10000100 216*0 8*9 8*0 8*d4 8*0 8*10000100 216*0 8*9 8*0 8*d4 8*0 8*10000100 216*0
  //   8*9 8*0 8*d4 8*0 8*10000100 216*0 8*9 8*0 8*d4 8*0 8*10000100 216*0 8*9 8*0 8*d4 8*0 8*10000100
  //   216*0 8*9 8*0 8*d4 8*0 8*10000100 216*0 8*9 8*0 8*d4 8*0 8*10000100 216*0 8*9 8*0 8*d4 8*0
  //   8*10000100 216*0 8*9 8*0 8*d4 8*0 8*10000100 216*0 8*9 8*0 8*d4 8*0 8*10000100 216*0 8*9 8*0 8*d4
  //   8*0 8*10000100 216*0 8*9 8*0 8*d4 8*0 8*10000100 216*0 8*9 8*0 8*d4 8*0 8*10000100 216*0 8*9 8*0
  //   8*d4 8*0 8*10000100 216*0 8*9 8*0 8*d4 8*0 8*10000100 216*0 8*9 8*0 8*d4 8*0 8*10000100 216*0 8*9
  //   8*0 8*d4 8*0 8*10000100 216*0 8*9 8*0 8*d4 8*0 8*10000100 216*0 8*9 8*0 8*d4 8*0 8*10000100 216*0
  //   8*9 8*0 8*d4 8*0 8*10000100 216*0 8*9 8*0 8*d4 8*0 8*10000100 216*0 8*9 8*0 8*d4 8*0 8*10000100
  //   216*0 8*9 8*0 8*d4 8*0 8*10000100 216*0 8*9 8*0 8*d4 8*0 8*10000100 216*0 8*9 8*0 8*d4 8*0
  //   8*10000100 216*0 8*9 8*0 8*d4 8*0 8*10000100 216*0 8*9 8*0 8*d4 8*0 8*10000100 216*0 8*9 8*0 8*d4
  //   8*0 8*10000100 216*0 8*9 8*0 8*d4 8*0 8*10000100 216*0 8*9 8*0 8*d4 8*0 8*10000100 216*0 8*9 8*0
  //   8*d4 8*0 8*10000100 216*0 8*9 8*0 8*d4 8*0 8*10000100 216*0 8*9 8*0 8*d4 8*0 8*10000100 216*0 8*9
  //   8*0 8*d4 8*0 8*10000100 216*0 8*9 8*0 8*d4 8*0 8*10000100 216*0 8*9 8*0 8*d4 8*0 8*10000100 216*0
  //   8*9 8*0 8*d4 8*0 8*10000100 216*0 8*9 8*0 8*d4 8*0 8*10000100 216*0 8*9 8*0 8*d4 8*0 8*10000100
  //   216*0 8*9 8*0 8*d4 8*0 8*10000100 216*0 8*9 8*0 8*d4 8*0 8*10000100 216*0 8*9 8*0 8*d4 8*0
  //   8*10000100 216*0 8*9 8*0 8*d4 8*0 8*10000100 216*0 8*9 8*0 8*d4 8*0 8*10000100 216*0 8*9 8*0 8*d4
  //   8*0 8*10000100 216*0 8*9 8*0 8*d4 8*0 8*10000100 216*0 8*9 8*0 8*d4 8*0 8*10000100 216*0 8*9 8*0
  //   8*d4 8*0 8*10000100 216*0 8*9 8*0 8*d4 8*0 8*10000100 216*0 8*9 8*0 8*d4 8*0 8*10000100 216*0 8*9
  //   8*0 8*d4 8*0 8*10000100 216*0 8*9 8*0 8*d4 8*0 8*10000100 216*0 8*9 8*0 8*d4 8*0 8*10000100 216*0
  //   8*9 8*0 8*d4 8*0 8*10000100 216*0 8*9 8*0 8*d4 8*0 8*10000100 216*0 8*9 8*0 8*d4 8*0 8*10000100
  //   216*0 8*9 8*0 8*d4 8*0 8*10000100 216*0 8*9 8*0 8*d4 8*0 8*10000100 216*0 8*9 8*0 8*d4 8*0
  //   8*10000100 216*0 8*9 8*0 8*d4 8*0 8*10000100 216*0 8*9 8*0 8*d4 8*0 8*10000100 216*0 8*9 8*0 8*d4
  //   8*0 8*10000100 216*0 8*9 8*0 8*d4 8*0 8*10000100 216*0 8*9 8*0 8*d4 8*0 8*10000100 216*0 8*9 8*0
  //   8*d4 8*0 8*10000100 216*0 8*9 8*0 8*d4 8*0 8*10000100 216*0 8*9 8*0 8*d4 8*0 8*10000100 216*0 8*9
  //   8*0 8*d4 8*0 8*10000100 216*0 8*9 8*0 8*d4 8*0 8*10000100 216*0 8*9 8*0 8*d4 8*0 8*10000100 216*0
  //   8*9 8*0 8*d4 8*0 8*10000100 216*0 8*9 8*0 8*d4 8*0 8*10000100 216*0 8*9 8*0 8*d4 8*0 8*10000100
  //   216*0 8*9 8*0 8*d4 8*0 8*10000100 216*0 8*9 8*0 8*d4 8*0 8*10000100 216*0 8*9 8*0 8*d4 8*0
  //   8*10000100 216*0 8*9 8*0 8*d4 8*0 8*10000100 216*0 8*9 8*0 8*d4 8*0 8*10000100 216*0 8*9 8*0 8*d4
  //   8*0 8*10000100 216*0 8*9 8*0 8*d4 8*0 8*10000100 216*0 8*9 8*0 8*d4 8*0 8*10000100 216*0 8*9 8*0
  //   8*d4 8*0 8*10000100 216*0 8*9 8*0 8*d4 8*0 8*10000100 216*0 8*9 8*0 8*d4 8*0 8*10000100 216*0 8*9
  //   8*0 8*d4 8*0 8*10000100 216*0 8*9 8*0 8*d4 8*0 8*10000100 216*0 8*9 8*0 8*d4 8*0 8*10000100 216*0
  //   8*9 8*0 8*d4 8*0 8*10000100 216*0 8*9 8*0 8*d4 8*0 8*10000100 216*0 8*9 8*0 8*d4 8*0 8*10000100
  //   216*0 8*9 8*0 8*d4 8*0 8*10000100 216*0 8*9 8*0 8*d4 8*0 8*10000100 216*0 8*9 8*0 8*d4 8*0
  //   8*10000100 216*0 8*9 8*0 8*d4 8*0 8*10000100 216*0 8*9 8*0 8*d4 8*0 8*10000100 216*0 8*9 8*0 8*d4
  //   8*0 8*10000100 216*0 8*9 8*0 8*d4 8*0 8*10000100 216*0 8*9 8*0 8*d4 8*0 8*10000100 216*0 8*9 8*0
  //   8*d4 8*0 8*10000100 216*0 8*9 8*0 8*d4 8*0 8*10000100 216*0 8*9 8*0 8*d4 8*0 8*10000100 216*0 8*9
  //   8*0 8*d4 8*0 8*10000100 216*0 8*9 8*0 8*d4 8*0 8*100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
endmodule
